# Fritzing sketch rpi-ultrasonic-servohat-example (saved by Fritzing 0.9.3b)

parts:
  Part1 = Adafruit 16-Channel PWM + Servo HAT [part_number="Adafruit #2327"]
  hc-sr1 = hc-sr04  # not connected
  R1 = Resistor [tolerance=±5% resistance=1k package=THT]
  R2 = Resistor [tolerance=±5% resistance=680 package=THT]

nets:
  N1: Part1.GPIO20, Part1.N$23, R1.Pin_0, R2.Pin_1
  N2: Part1.GND, R1.Pin_1
  N3: Part1.N$41, R2.Pin_0

custom parts:
  Adafruit 16-Channel PWM + Servo HAT: The Raspberry Pi is a wonderful little computer, but one thing it isn't very good at is controlling DC Servo Motors - these motors need very specific and repetitive timing pulses to set the position. Instead of asking the Pi Linux kernel to send these signals, pop on this handy HAT! It adds the capability to control 16 Servos with perfect timing. It can also do PWM up to 1.6 KHz with 12 bit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

// code stored in the sketch: UltrasonicServoHatOldSchool.ino
import RPi.GPIO as GPIO
import time
GPIO.setmode(GPIO.BOARD)

#set GPIO Pins
GPIO_TRIGGER = 40
GPIO_ECHO = 38
 
#set GPIO direction (IN / OUT)
GPIO.setup(GPIO_TRIGGER, GPIO.OUT)
GPIO.setup(GPIO_ECHO, GPIO.IN)
 
def distance():
    # set Trigger to HIGH
    GPIO.output(GPIO_TRIGGER, True)
 
    # set Trigger after 0.01ms to LOW
    time.sleep(0.00001)
    GPIO.output(GPIO_TRIGGER, False)
 
    StartTime = time.time()
    StopTime = time.time()
 
    # save StartTime
    while GPIO.input(GPIO_ECHO) == 0:
        StartTime = time.time()
 
    # save time of arrival
    while GPIO.input(GPIO_ECHO) == 1:
        StopTime = time.time()
 
    # time difference between start and arrival
    TimeElapsed = StopTime - StartTime
    # multiply with the sonic speed (34300 cm/s)
    # and divide by 2, because there and back
    distance = (TimeElapsed * 34300) / 2
 
    return distance
 
if __name__ == '__main__':
    try:
        while True:
            dist = distance()
            print ("Measured Distance = %.1f cm" % dist)
            time.sleep(1)
 
        # Reset by pressing CTRL + C
    except KeyboardInterrupt:
        print("Measurement stopped by User")
        GPIO.cleanup()
